// Logisim project Calculatrice.circ as structural Verilog
module _7seg (
  input  A,
  input  B,
  input  C,
  input  D
);

  wire and_1_out, and_2_out, not_1_out, not_2_out, or_1_out, or_2_out, or_3_out;

  or or_1 (or_1_out, A, C);
  not not_1 (not_1_out, B);
  and and_1 (and_1_out, B, D);
  or or_2 (or_2_out, and_1_out, and_2_out);
  or or_3 (or_3_out, or_1_out, or_2_out);
  LED led_1 (.in(or_3_out));
  not not_2 (not_2_out, D);
  and and_2 (and_2_out, not_1_out, not_2_out);
endmodule
